// Logisim project BE 1.circ as structural Verilog
module Demi___additionneur (
);

  wire button_1_out, button_2_out;

  Button button_1 (.out(button_1_out));
  Button button_2 (.out(button_2_out));
  // AND_Gate and_1 is placed but not wired
  // XOR_Gate xor_1 has open pins: in0=button_1_out, in4=button_2_out, out=open
endmodule
